// Logisim project Division.circ as structural Verilog: 1 circuit, main circuit main
// b2
module main (
  input  a0,
  input  a1,
  input  a2,
  input  a3,
  input  a4,
  input  b0,
  input  b1,
  input  b2,
  input  b3,
  input  b4,
  output Q3,
  output Q2,
  output Q0,
  output Q1
);

  wire and_1_out, and_2_out, and_3_out, and_4_out, and_5_out, and_6_out, and_7_out, and_8_out, and_9_out,
       and_10_out, and_11_out, and_12_out, and_13_out, and_14_out, and_15_out, and_16_out, comparator_1_p3,
       comparator_1_p6, comparator_2_p3, comparator_2_p6, comparator_3_p3, comparator_3_p6, comparator_4_p3,
       comparator_4_p6, main_1_p1, main_1_p3, main_1_p5, main_2_p1, main_2_p3, main_2_p5, main_3_p1,
       main_3_p3, main_3_p5, n2_1_mux_1_p4, n2_1_mux_3_p4, not_1_out, not_2_out, or_2_out, or_3_out,
       or_4_out, or_5_out, or_6_out, or_7_out, or_8_out, or_10_out, xor_1_out;

  xor xor_1 (xor_1_out, a4, b4);
  // comparator comparator_1: pin names not known; wires that end beside it: 1'b0, 1'b0, comparator_1_p3, 1'b0, a3, comparator_1_p6, b3, b2, b1, b0
  LED sign_flag_Q4 (.in(xor_1_out));
  // _2_1_mux 2_1_mux_1: pin names not known; wires that end beside it: Q3, 1'b0, 1'b1, n2_1_mux_1_p4
  or or_1 (n2_1_mux_1_p4, comparator_1_p3, comparator_1_p6);
  or or_2 (or_2_out, a0, a1);
  or or_3 (or_3_out, a2, a3);
  and and_1 (and_1_out, Q3, b0);
  and and_2 (and_2_out, Q3, b1);
  and and_3 (and_3_out, Q3, b2);
  and and_4 (and_4_out, Q3, b3);
  or or_4 (or_4_out, or_2_out, or_3_out);
  not not_1 (not_1_out, or_4_out);
  // subtractor_main main_1: pin names not known; wires that end beside it: main_1_p1, and_1_out, main_1_p3, and_2_out, main_1_p5, and_3_out, and_4_out, a3, 1'b0, 1'b0, 1'b0
  LED result_0 (.in(not_1_out));
  or or_5 (or_5_out, b3, b2);
  or or_6 (or_6_out, b1, b0);
  // comparator comparator_2: pin names not known; wires that end beside it: main_1_p5, main_1_p3, comparator_2_p3, main_1_p1, a2, comparator_2_p6, b3, b2, b1, b0
  or or_7 (or_7_out, comparator_2_p3, comparator_2_p6);
  not not_2 (not_2_out, or_8_out);
  or or_8 (or_8_out, or_5_out, or_6_out);
  // _2_1_mux 2_1_mux_2: pin names not known; wires that end beside it: Q2, 1'b0, 1'b1, or_7_out
  LED divison_by_0 (.in(not_2_out));
  and and_5 (and_5_out, Q2, b0);
  and and_6 (and_6_out, Q2, b1);
  and and_7 (and_7_out, Q2, b2);
  and and_8 (and_8_out, Q2, b3);
  // subtractor_main main_2: pin names not known; wires that end beside it: main_2_p1, and_5_out, main_2_p3, and_6_out, main_2_p5, and_7_out, and_8_out, a2, main_1_p1, main_1_p3, main_1_p5
  // comparator comparator_3: pin names not known; wires that end beside it: main_2_p5, main_2_p3, comparator_3_p3, main_2_p1, a1, comparator_3_p6, b3, b2, b1, b0
  // _2_1_mux 2_1_mux_3: pin names not known; wires that end beside it: Q1, 1'b0, 1'b1, n2_1_mux_3_p4
  or or_9 (n2_1_mux_3_p4, comparator_3_p3, comparator_3_p6);
  and and_9 (and_9_out, Q1, b0);
  and and_10 (and_10_out, Q1, b1);
  and and_11 (and_11_out, Q1, b2);
  and and_12 (and_12_out, Q1, b3);
  // subtractor_main main_3: pin names not known; wires that end beside it: main_3_p1, and_9_out, main_3_p3, and_10_out, main_3_p5, and_11_out, and_12_out, a1, main_2_p1, main_2_p3, main_2_p5
  // comparator comparator_4: pin names not known; wires that end beside it: main_3_p5, main_3_p3, comparator_4_p3, main_3_p1, a0, comparator_4_p6, b3, b2, b1, b0
  or or_10 (or_10_out, comparator_4_p3, comparator_4_p6);
  // _2_1_mux 2_1_mux_4: pin names not known; wires that end beside it: Q0, 1'b0, 1'b1, or_10_out
  and and_13 (and_13_out, Q0, b0);
  and and_14 (and_14_out, Q0, b1);
  and and_15 (and_15_out, Q0, b2);
  and and_16 (and_16_out, Q0, b3);
  // subtractor_main main_4: pin names not known; wires that end beside it: and_13_out, and_14_out, and_15_out, and_16_out, a0, main_3_p1, main_3_p3, main_3_p5
endmodule
