// Logisim project Full Adder.circ as structural Verilog: 1 circuit, main circuit Full Adder
module Full_Adder (
  input  In1,
  input  In2,
  input  In3,
  output S,
  output C
);

  wire half_adder_1_c, half_adder_1_s, half_adder_2_c;

  Half_Adder half_adder_1 (.I1(In1), .I2(In2), .S(half_adder_1_s), .C(half_adder_1_c));
  Half_Adder half_adder_2 (.I1(half_adder_1_s), .I2(In3), .S(S), .C(half_adder_2_c));
  or or_1 (C, half_adder_2_c, half_adder_1_c);
endmodule
