// Logisim project MULTIPLICATION.circ as structural Verilog: 1 circuit, main circuit main
module main (
  input  B4,
  input  B3,
  input  B2,
  input  B1,
  input  B0,
  input  A0,
  input  A1,
  input  A2,
  input  A3,
  input  A4,
  output Sign,
  output L8,
  output L7,
  output L6,
  output L5,
  output L4,
  output L3,
  output L2,
  output L1,
  output Result_0
);

  wire and_1_out, and_2_out, and_3_out, and_4_out, and_5_out, and_6_out, and_7_out, and_8_out, and_9_out,
       and_10_out, and_11_out, and_12_out, and_13_out, and_14_out, and_15_out, full_adder_2_c,
       full_adder_2_s, full_adder_3_c, full_adder_4_c, full_adder_4_s, full_adder_5_c, full_adder_5_s,
       full_adder_6_c, full_adder_7_c, full_adder_7_s, full_adder_8_c, full_adder_8_s, full_adder_9_c,
       full_adder_10_c, full_adder_10_s, full_adder_11_c, full_adder_12_c, or_1_out, or_2_out, or_3_out,
       or_4_out, or_5_out, or_6_out, or_7_out;

  xor xor_1 (Sign, A4, B4);
  and and_1 (and_1_out, B3, A3);
  or or_1 (or_1_out, L8, L7);
  and and_2 (and_2_out, B3, A2);
  and and_3 (and_3_out, B2, A3);
  Full_Adder full_adder_1 (.In1(full_adder_3_c), .In2(full_adder_2_c), .In3(and_1_out), .S(L7), .C(L8));
  or or_2 (or_2_out, or_1_out, or_3_out);
  Full_Adder full_adder_2 (
    .In1(full_adder_5_c), .In2(full_adder_4_c), .In3(and_2_out), .S(full_adder_2_s), .C(full_adder_2_c));
  Full_Adder full_adder_3 (.In1(full_adder_6_c), .In2(full_adder_2_s), .In3(and_3_out), .S(L6), .C(full_adder_3_c));
  and and_4 (and_4_out, B3, A1);
  and and_5 (and_5_out, B2, A2);
  and and_6 (and_6_out, B1, A3);
  or or_3 (or_3_out, L6, L5);
  Full_Adder full_adder_4 (.In1(full_adder_7_c), .In2(1'b0), .In3(and_4_out), .S(full_adder_4_s), .C(full_adder_4_c));
  Full_Adder full_adder_5 (
    .In1(full_adder_8_c), .In2(full_adder_4_s), .In3(and_5_out), .S(full_adder_5_s), .C(full_adder_5_c));
  Full_Adder full_adder_6 (.In1(full_adder_9_c), .In2(full_adder_5_s), .In3(and_6_out), .S(L5), .C(full_adder_6_c));
  and and_7 (and_7_out, B2, A1);
  and and_8 (and_8_out, B1, A2);
  and and_9 (and_9_out, B0, A3);
  or or_4 (or_4_out, or_2_out, or_6_out);
  not not_1 (Result_0, or_4_out);
  and and_10 (and_10_out, B3, A0);
  Full_Adder full_adder_7 (
    .In1(full_adder_10_c), .In2(and_10_out), .In3(and_7_out), .S(full_adder_7_s), .C(full_adder_7_c));
  Full_Adder full_adder_8 (
    .In1(full_adder_11_c), .In2(full_adder_7_s), .In3(and_8_out), .S(full_adder_8_s), .C(full_adder_8_c));
  and and_11 (and_11_out, B1, A1);
  and and_12 (and_12_out, B0, A2);
  Full_Adder full_adder_9 (.In1(1'b0), .In2(full_adder_8_s), .In3(and_9_out), .S(L4), .C(full_adder_9_c));
  and and_13 (and_13_out, B2, A0);
  or or_5 (or_5_out, L4, L3);
  Full_Adder full_adder_10 (
    .In1(full_adder_12_c), .In2(and_13_out), .In3(and_11_out), .S(full_adder_10_s), .C(full_adder_10_c));
  Full_Adder full_adder_11 (.In1(1'b0), .In2(full_adder_10_s), .In3(and_12_out), .S(L3), .C(full_adder_11_c));
  and and_14 (and_14_out, B0, A1);
  or or_6 (or_6_out, or_5_out, or_7_out);
  and and_15 (and_15_out, B1, A0);
  Full_Adder full_adder_12 (.In1(1'b0), .In2(and_15_out), .In3(and_14_out), .S(L2), .C(full_adder_12_c));
  or or_7 (or_7_out, L2, L1);
  and and_16 (L1, B0, A0);
endmodule
