// Logisim project Project.circ as structural Verilog: 2 circuits, main circuit main
module main (
  input  S1,
  input  S0,
  input  a0,
  input  a1,
  input  a2,
  input  a3,
  input  a4,
  input  b0,
  input  b1,
  input  b2,
  input  b3,
  input  b4
);

  wire alu_1_division_by_zero, alu_1_out_13, alu_1_out_14, alu_1_out_15, alu_1_out_16, alu_1_out_17,
       alu_1_out_18, alu_1_out_19, alu_1_out_20, alu_1_sign, alu_1_zero_result, bcd_to_7_segment_1_a,
       bcd_to_7_segment_1_b, bcd_to_7_segment_1_c, bcd_to_7_segment_1_d, bcd_to_7_segment_1_e,
       bcd_to_7_segment_1_f, bcd_to_7_segment_1_g, bcd_to_7_segment_2_a, bcd_to_7_segment_2_b,
       bcd_to_7_segment_2_c, bcd_to_7_segment_2_d, bcd_to_7_segment_2_e, bcd_to_7_segment_2_f,
       bcd_to_7_segment_2_g, bcd_to_7_segment_3_a, bcd_to_7_segment_3_b, bcd_to_7_segment_3_c,
       bcd_to_7_segment_3_d, bcd_to_7_segment_3_e, bcd_to_7_segment_3_f, bcd_to_7_segment_3_g, bitobcd_1_h1,
       bitobcd_1_h2, bitobcd_1_h3, bitobcd_1_h4, bitobcd_1_t1, bitobcd_1_t2, bitobcd_1_t3, bitobcd_1_t4,
       bitobcd_1_u1, bitobcd_1_u2, bitobcd_1_u3, bitobcd_1_u4;

  LED led_1 (.in(alu_1_sign));
  ALU alu_1 (
    .s1(S1), .S0(S0), .a0(a0), .a1(a1), .a2(a2), .a3(a3), .a4(a4), .b0(b0), .b1(b1), .b2(b2), .b3(b3),
    .b4(b4), .division_by_zero(alu_1_division_by_zero), .zero_result(alu_1_zero_result), .Sign(alu_1_sign),
    .out_13(alu_1_out_13), .out_14(alu_1_out_14), .out_15(alu_1_out_15), .out_16(alu_1_out_16),
    .out_17(alu_1_out_17), .out_18(alu_1_out_18), .out_19(alu_1_out_19), .out_20(alu_1_out_20));
  BITOBCD bitobcd_1 (
    ._8(alu_1_out_20), ._7(alu_1_out_19), ._6(alu_1_out_18), ._5(alu_1_out_17), ._4(alu_1_out_16),
    ._3(alu_1_out_15), ._2(alu_1_out_14), ._1(alu_1_out_13), .H4(bitobcd_1_h4), .H3(bitobcd_1_h3),
    .H2(bitobcd_1_h2), .H1(bitobcd_1_h1), .T4(bitobcd_1_t4), .T3(bitobcd_1_t3), .T2(bitobcd_1_t2),
    .T1(bitobcd_1_t1), .U4(bitobcd_1_u4), .U3(bitobcd_1_u3), .U2(bitobcd_1_u2), .U1(bitobcd_1_u1));
  LED led_2 (.in(alu_1_division_by_zero));
  LED led_3 (.in(alu_1_zero_result));
  bcd_to_7_segment bcd_to_7_segment_1 (
    .w(bitobcd_1_u4), .x(bitobcd_1_u3), .y(bitobcd_1_u2), .z(bitobcd_1_u1), .a(bcd_to_7_segment_1_a),
    .b(bcd_to_7_segment_1_b), .c(bcd_to_7_segment_1_c), .d(bcd_to_7_segment_1_d), .e(bcd_to_7_segment_1_e),
    .f(bcd_to_7_segment_1_f), .g(bcd_to_7_segment_1_g));
  bcd_to_7_segment bcd_to_7_segment_2 (
    .w(bitobcd_1_t4), .x(bitobcd_1_t3), .y(bitobcd_1_t2), .z(bitobcd_1_t1), .a(bcd_to_7_segment_2_a),
    .b(bcd_to_7_segment_2_b), .c(bcd_to_7_segment_2_c), .d(bcd_to_7_segment_2_d), .e(bcd_to_7_segment_2_e),
    .f(bcd_to_7_segment_2_f), .g(bcd_to_7_segment_2_g));
  bcd_to_7_segment bcd_to_7_segment_3 (
    .w(bitobcd_1_h4), .x(bitobcd_1_h3), .y(bitobcd_1_h2), .z(bitobcd_1_h1), .a(bcd_to_7_segment_3_a),
    .b(bcd_to_7_segment_3_b), .c(bcd_to_7_segment_3_c), .d(bcd_to_7_segment_3_d), .e(bcd_to_7_segment_3_e),
    .f(bcd_to_7_segment_3_f), .g(bcd_to_7_segment_3_g));
  _7_Segment_Display u_7_segment_display_1 (
    .g(bcd_to_7_segment_1_g), .f(bcd_to_7_segment_1_f), .a(bcd_to_7_segment_1_a), .b(bcd_to_7_segment_1_b),
    .e(bcd_to_7_segment_1_e), .d(bcd_to_7_segment_1_d), .c(bcd_to_7_segment_1_c));  // open: dp
  _7_Segment_Display u_7_segment_display_2 (
    .g(bcd_to_7_segment_2_g), .f(bcd_to_7_segment_2_f), .a(bcd_to_7_segment_2_a), .b(bcd_to_7_segment_2_b),
    .e(bcd_to_7_segment_2_e), .d(bcd_to_7_segment_2_d), .c(bcd_to_7_segment_2_c));  // open: dp
  _7_Segment_Display u_7_segment_display_3 (
    .g(bcd_to_7_segment_3_g), .f(bcd_to_7_segment_3_f), .a(bcd_to_7_segment_3_a), .b(bcd_to_7_segment_3_b),
    .e(bcd_to_7_segment_3_e), .d(bcd_to_7_segment_3_d), .c(bcd_to_7_segment_3_c));  // open: dp

  // Notes on the sheet:
  //   Addition
  //   5-3=2
  //   5+3=8
  //   -5-3=-8
  //   -5+2=-3
  //   Subtraction
  //   -5-(-3)=-2
  //   -2-(-5)=3
  //   5-(-3)=8
  //   2-(-5)=7
  //   Multiplication
  //   1x2=2
  //   15x-3=-45
  //   -2x6=-12
  //   -4x-3=12
  //   Division
  //   -2/1=-2
  //   5/2=2
  //   9/-3=-3
  //   15/0=?
  //   -6/-2=3
  //   S1    S0
  //   Additon 00
  //   Sutraction 01
  //   Multiplication 10
  //   Division 11
  //   Sign
  //   Result=0
  //   Division by zero
  //   units
  //   tens
  //   hundreds
endmodule

module ALU (
  input  s1,
  input  S0,
  input  a0,
  input  a1,
  input  a2,
  input  a3,
  input  a4,
  input  b0,
  input  b1,
  input  b2,
  input  b3,
  input  b4,
  output out_13,
  output out_14,
  output out_15,
  output out_16,
  output out_17,
  output out_18,
  output out_19,
  output out_20,
  output division_by_zero,
  output zero_result,
  output Sign
);

  wire main_1_p9, main_1_p10, main_1_p11, main_1_p12, main_1_p15, main_1_p16, main_1_p17, main_2_p12,
       main_2_p13, main_2_p14, main_2_p15, main_2_p16, main_2_p17, main_2_p18, mult_1_l1, mult_1_l2,
       mult_1_l3, mult_1_l4, mult_1_l5, mult_1_l6, mult_1_l7, mult_1_l8, mult_1_result_0, mult_1_sign;

  MULT mult_1 (
    .B4(b4), .B3(b3), .B2(b2), .B1(b1), .B0(b0), .A0(a0), .A1(a1), .A2(a2), .A3(a3), .A4(a4),
    .Sign(mult_1_sign), .L8(mult_1_l8), .L7(mult_1_l7), .L6(mult_1_l6), .L5(mult_1_l5),
    .Result_0(mult_1_result_0), .L4(mult_1_l4), .L3(mult_1_l3), .L2(mult_1_l2), .L1(mult_1_l1));
  // Integer_Division_main main_1: pin names not known; wires that end beside it: a0, a1, a2, a3, b0, b1, b2, b3, main_1_p9, main_1_p10, main_1_p11, main_1_p12, a4, b4, main_1_p15, main_1_p16, main_1_p17
  // add_sub_main main_2: pin names not known; wires that end beside it: a0, a1, a2, a3, a4, b0, b1, b2, b3, b4, S0, main_2_p12, main_2_p13, main_2_p14, main_2_p15, main_2_p16, main_2_p17, main_2_p18
  _4_1MUX u_4_1mux_1 (.I0(1'b0), .I1(1'b0), .I2(1'b0), .I3(main_1_p15), .S1(s1), .S0(S0), .O(division_by_zero));
  _4_1MUX u_4_1mux_2 (.I0(main_2_p12), .I1(main_2_p12), .I2(mult_1_sign), .I3(main_1_p16), .S1(s1), .S0(S0), .O(Sign));
  _4_1MUX u_4_1mux_3 (
    .I0(main_2_p18), .I1(main_2_p18), .I2(mult_1_result_0), .I3(main_1_p17), .S1(s1), .S0(S0), .O(zero_result));
  _4_1MUX u_4_1mux_4 (.I0(main_2_p16), .I1(main_2_p16), .I2(mult_1_l1), .I3(main_1_p12), .S1(s1), .S0(S0), .O(out_13));
  _4_1MUX u_4_1mux_5 (.I0(main_2_p14), .I1(main_2_p14), .I2(mult_1_l2), .I3(main_1_p11), .S1(s1), .S0(S0), .O(out_14));
  _4_1MUX u_4_1mux_6 (.I0(main_2_p13), .I1(main_2_p13), .I2(mult_1_l3), .I3(main_1_p10), .S1(s1), .S0(S0), .O(out_15));
  _4_1MUX u_4_1mux_7 (.I0(main_2_p15), .I1(main_2_p15), .I2(mult_1_l4), .I3(main_1_p9), .S1(s1), .S0(S0), .O(out_16));
  _4_1MUX u_4_1mux_8 (.I0(main_2_p17), .I1(main_2_p17), .I2(mult_1_l5), .I3(1'b0), .S1(s1), .S0(S0), .O(out_17));
  _4_1MUX u_4_1mux_9 (.I0(1'b0), .I1(1'b0), .I2(mult_1_l6), .I3(1'b0), .S1(s1), .S0(S0), .O(out_18));
  _4_1MUX u_4_1mux_10 (.I0(1'b0), .I1(1'b0), .I2(mult_1_l7), .I3(1'b0), .S1(s1), .S0(S0), .O(out_19));
  _4_1MUX u_4_1mux_11 (.I0(1'b0), .I1(1'b0), .I2(mult_1_l8), .I3(1'b0), .S1(s1), .S0(S0), .O(out_20));

  // Notes on the sheet:
  //   Mult
endmodule
