// Logisim project add_sub.circ as structural Verilog: 7 circuits, main circuit main
module main (
  input  a0,
  input  a1,
  input  a2,
  input  a3,
  input  a4,
  input  b0,
  input  b1,
  input  b2,
  input  b3,
  input  b4,
  input  in_11,
  output s5,
  output s2,
  output s1,
  output s3,
  output s0,
  output s4
);

  wire comparator_1_a_b, comparator_1_a_b_2, comparator_1_a_b_3, full_adder_1_y, full_adder_2_y,
       full_adder_3_y, full_adder_4_y, n2_1_mux_1_out_4, n2_1_mux_2_out_4, n2_1_mux_3_out_4,
       n2_1_mux_4_out_4, n2_1_mux_5_out_4, n2_1_mux_6_out_4, n2_1_mux_7_out_4, n2_1_mux_8_out_4,
       n2_1_mux_11_out_4, not_1_out, xor_1_out, xor_2_out, xor_3_out, xor_4_out, xor_5_out, xor_6_out;

  comparator comparator_1 (
    .a3(a3), .a2(a2), .a1(a1), .a0(a0), .b3(b3), .b2(b2), .b1(b1), .b0(b0), .a_b(comparator_1_a_b),
    .a_b_2(comparator_1_a_b_2), .a_b_3(comparator_1_a_b_3));
  _2_1_mux u_2_1_mux_1 (.d0(b0), .d1(a0), .select(comparator_1_a_b_3), .out_4(n2_1_mux_1_out_4));
  _2_1_mux u_2_1_mux_2 (.d0(b0), .d1(a0), .select(comparator_1_a_b_2), .out_4(n2_1_mux_2_out_4));
  xor xor_1 (xor_1_out, n2_1_mux_2_out_4, xor_2_out);
  xor xor_2 (xor_2_out, in_11, xor_3_out);
  xor xor_3 (xor_3_out, b4, a4);
  _2_1_mux u_2_1_mux_3 (.d0(b1), .d1(a1), .select(comparator_1_a_b_3), .out_4(n2_1_mux_3_out_4));
  _2_1_mux u_2_1_mux_4 (.d0(b1), .d1(a1), .select(comparator_1_a_b_2), .out_4(n2_1_mux_4_out_4));
  full_adder full_adder_1 (.a(n2_1_mux_1_out_4), .b(xor_1_out), .c(xor_2_out), .x(s0), .y(full_adder_1_y));
  xor xor_4 (xor_4_out, n2_1_mux_4_out_4, xor_2_out);
  _2_1_mux u_2_1_mux_5 (.d0(b2), .d1(a2), .select(comparator_1_a_b_3), .out_4(n2_1_mux_5_out_4));
  _2_1_mux u_2_1_mux_6 (.d0(b2), .d1(a2), .select(comparator_1_a_b_2), .out_4(n2_1_mux_6_out_4));
  full_adder full_adder_2 (.a(n2_1_mux_3_out_4), .b(xor_4_out), .c(full_adder_1_y), .x(s1), .y(full_adder_2_y));
  full_adder full_adder_3 (.a(n2_1_mux_5_out_4), .b(xor_5_out), .c(full_adder_2_y), .x(s2), .y(full_adder_3_y));
  xor xor_5 (xor_5_out, n2_1_mux_6_out_4, xor_2_out);
  _2_1_mux u_2_1_mux_7 (.d0(b3), .d1(a3), .select(comparator_1_a_b_3), .out_4(n2_1_mux_7_out_4));
  _2_1_mux u_2_1_mux_8 (.d0(b3), .d1(a3), .select(comparator_1_a_b_2), .out_4(n2_1_mux_8_out_4));
  _2_1_mux u_2_1_mux_9 (.d0(n2_1_mux_11_out_4), .d1(a4), .select(comparator_1_a_b_3), .out_4(s5));
  xor xor_6 (xor_6_out, n2_1_mux_8_out_4, xor_2_out);
  full_adder full_adder_4 (.a(n2_1_mux_7_out_4), .b(xor_6_out), .c(full_adder_3_y), .x(s3), .y(full_adder_4_y));
  _2_1_mux u_2_1_mux_10 (.d0(1'b0), .d1(full_adder_4_y), .select(xor_3_out), .out_4(s4));
  _2_1_mux u_2_1_mux_11 (.d0(b4), .d1(not_1_out), .select(in_11), .out_4(n2_1_mux_11_out_4));
  not not_1 (not_1_out, b4);
endmodule

module half_adder (
  input  a,
  input  b,
  output x,
  output y
);

  xor xor_1 (x, a, b);
  and and_1 (y, a, b);
endmodule

module full_adder (
  input  a,
  input  b,
  input  c,
  output x,
  output y
);

  wire and_1_out, and_2_out, and_3_out, and_4_out, and_5_out, and_6_out, and_7_out, not_1_out, not_2_out,
       not_3_out, not_4_out, not_5_out, not_6_out;

  not not_1 (not_1_out, a);
  not not_2 (not_2_out, b);
  not not_3 (not_3_out, a);
  not not_4 (not_4_out, c);
  not not_5 (not_5_out, b);
  not not_6 (not_6_out, c);
  and and_1 (and_1_out, b, c);
  and and_2 (and_2_out, a, c);
  and and_3 (and_3_out, a, b);
  and and_4 (and_4_out, not_1_out, not_2_out, c);
  and and_5 (and_5_out, not_3_out, b, not_4_out);
  and and_6 (and_6_out, a, not_5_out, not_6_out);
  and and_7 (and_7_out, a, b, c);
  or or_1 (y, and_1_out, and_2_out, and_3_out);
  or or_2 (x, and_4_out, and_5_out, and_6_out, and_7_out);

  // Notes on the sheet:
  //   sum
  //   carry
endmodule

module comparator (
  input  a3,
  input  a2,
  input  a1,
  input  a0,
  input  b3,
  input  b2,
  input  b1,
  input  b0,
  output a_b,
  output a_b_2,
  output a_b_3
);

  wire and_1_out, and_3_out, and_4_out, and_5_out, and_6_out, nand_1_out, not_1_out, not_2_out, not_3_out,
       not_4_out, not_5_out, not_6_out, not_7_out, not_8_out, not_9_out, xor_1_out, xor_2_out, xor_3_out,
       xor_4_out;

  xor xor_1 (xor_1_out, a3, b3);
  xor xor_2 (xor_2_out, a2, b2);
  xor xor_3 (xor_3_out, a1, b1);
  xor xor_4 (xor_4_out, a0, b0);
  not not_1 (not_1_out, xor_1_out);
  not not_2 (not_2_out, xor_2_out);
  not not_3 (not_3_out, xor_3_out);
  not not_4 (not_4_out, b3);
  not not_5 (not_5_out, b2);
  not not_6 (not_6_out, b1);
  not not_7 (not_7_out, b0);
  not not_8 (not_8_out, xor_4_out);
  and and_1 (and_1_out, not_1_out, not_2_out);
  and and_2 (a_b, and_1_out, and_3_out);
  and and_3 (and_3_out, not_3_out, not_8_out);
  and and_4 (and_4_out, not_4_out, a3);
  and and_5 (and_5_out, not_1_out, not_5_out, a2);
  and and_6 (and_6_out, not_2_out, not_1_out, a1, not_6_out);
  nand nand_1 (nand_1_out, not_1_out, not_2_out, not_3_out, not_7_out, a0);
  or or_1 (a_b_3, and_4_out, and_5_out, and_6_out, not_9_out);
  not not_9 (not_9_out, nand_1_out);
  nor nor_1 (a_b_2, a_b, a_b_3);
endmodule

module _2_1_mux (
  input  d0,
  input  d1,
  input  select,
  output out_4
);

  wire and_1_out, and_2_out, not_1_out;

  not not_1 (not_1_out, select);
  and and_1 (and_1_out, d0, not_1_out);
  and and_2 (and_2_out, d1, select);
  or or_1 (out_4, and_1_out, and_2_out);
endmodule

module bcd_to_7_segment (
  input  w,
  input  x,
  input  y,
  input  z,
  output a,
  output b,
  output c,
  output d,
  output e,
  output f,
  output g
);

  wire and_1_out, and_2_out, and_3_out, and_4_out, and_5_out, and_6_out, and_7_out, and_8_out, and_9_out,
       and_10_out, and_11_out, and_12_out, and_13_out, and_14_out, and_15_out, and_16_out, and_17_out,
       and_19_out, not_1_out, not_2_out, not_3_out, not_4_out, or_2_out, or_3_out, or_4_out, or_5_out,
       or_6_out, or_7_out, or_8_out, or_9_out, or_12_out, or_13_out, or_14_out, or_15_out, or_18_out,
       xnor_1_out, xnor_2_out;

  not not_1 (not_1_out, w);
  not not_2 (not_2_out, x);
  not not_3 (not_3_out, y);
  not not_4 (not_4_out, z);
  xnor xnor_1 (xnor_1_out, x, z);
  or or_1 (a, xnor_1_out, or_2_out);
  or or_2 (or_2_out, w, y);
  or or_3 (or_3_out, w, not_2_out);
  xnor xnor_2 (xnor_2_out, y, z);
  or or_4 (or_4_out, w, not_3_out);
  or or_5 (or_5_out, z, x);
  and and_1 (and_1_out, w, w);
  and and_2 (and_2_out, not_2_out, not_4_out);
  and and_3 (and_3_out, not_2_out, y);
  or or_6 (or_6_out, and_3_out, and_4_out);
  and and_4 (and_4_out, y, not_4_out);
  and and_5 (and_5_out, x, x);
  and and_6 (and_6_out, and_5_out, and_7_out);
  and and_7 (and_7_out, not_3_out, z);
  or or_7 (or_7_out, y, not_2_out);
  and and_8 (and_8_out, w, w);
  or or_8 (or_8_out, not_4_out, x);
  and and_9 (and_9_out, or_8_out, not_3_out);
  and and_10 (and_10_out, not_1_out, x);
  and and_11 (and_11_out, y, not_4_out);
  and and_12 (and_12_out, w, w);
  or or_9 (or_9_out, and_12_out, and_13_out);
  and and_13 (and_13_out, x, not_3_out);
  and and_14 (and_14_out, y, not_4_out);
  and and_15 (and_15_out, not_1_out, not_2_out);
  and and_16 (and_16_out, and_15_out, and_17_out);
  and and_17 (and_17_out, y, y);
  or or_10 (b, or_3_out, xnor_2_out);
  or or_11 (c, or_4_out, or_5_out);
  or or_12 (or_12_out, and_1_out, and_2_out);
  or or_13 (or_13_out, or_12_out, or_6_out);
  or or_14 (or_14_out, and_6_out, and_6_out);
  and and_18 (e, or_7_out, not_4_out);
  or or_15 (or_15_out, and_8_out, and_9_out);
  or or_16 (f, or_15_out, and_19_out);
  and and_19 (and_19_out, and_10_out, and_11_out);
  or or_17 (g, or_9_out, or_18_out);
  or or_18 (or_18_out, and_14_out, and_16_out);
  or or_19 (d, or_13_out, or_14_out);
endmodule

module check (
  input  in_1,
  input  in_2,
  input  in_3,
  input  in_4
);

  wire bcd_to_7_segment_1_a, bcd_to_7_segment_1_b, bcd_to_7_segment_1_c, bcd_to_7_segment_1_d,
       bcd_to_7_segment_1_e, bcd_to_7_segment_1_f, bcd_to_7_segment_1_g;

  bcd_to_7_segment bcd_to_7_segment_1 (
    .w(in_1), .x(in_2), .y(in_3), .z(in_4), .a(bcd_to_7_segment_1_a), .b(bcd_to_7_segment_1_b),
    .c(bcd_to_7_segment_1_c), .d(bcd_to_7_segment_1_d), .e(bcd_to_7_segment_1_e), .f(bcd_to_7_segment_1_f),
    .g(bcd_to_7_segment_1_g));
  _7_Segment_Display u_7_segment_display_1 (
    .g(bcd_to_7_segment_1_g), .f(bcd_to_7_segment_1_f), .a(bcd_to_7_segment_1_a), .b(bcd_to_7_segment_1_b),
    .e(bcd_to_7_segment_1_e), .d(bcd_to_7_segment_1_d), .c(bcd_to_7_segment_1_c));  // open: dp
endmodule
